# Fritzing sketch EHP2 (saved by Fritzing 1.0.5)
breadboards: 1

parts:
  Pico/Pico2_Mod_1 = Raspberry Pi Pico or Pico 2
  S1 = Pushbutton [package="[THT]"]
  S2 = Pushbutton [package="[THT]"]
  S3 = Pushbutton [package="[THT]"]
  S4 = Pushbutton [package="[THT]"]
  LED1 = smd LED [color="Red (633nm)" package="0603 [SMD]"]
  LED2 = smd LED [color="Green (555nm)" package="0603 [SMD]"]
  LED4 = smd LED [color="Yellow (595nm)" package="0603 [SMD]"]
  R3 = Resistor [tolerance=±5% power=0.25W resistance=220 package=THT]
  R4 = Resistor [tolerance=±5% power=0.25W resistance=220 package=THT]
  R5 = Resistor [tolerance=±5% power=0.25W resistance=220 package=THT]
  IR1 = TSOP312.., 314.. [package=THT]  # not connected
  DHT11_1 = DHT11 module  # not connected
  J1 = Basic Servo

nets:
  N1: Pico/Pico2_Mod_1.pin_3, Pico/Pico2_Mod_1.pin_8, Pico/Pico2_Mod_1.pin_13, Pico/Pico2_Mod_1.pin_18, Pico/Pico2_Mod_1.pin_23, Pico/Pico2_Mod_1.pin_28, Pico/Pico2_Mod_1.pin_33, Pico/Pico2_Mod_1.pin_38, Pico/Pico2_Mod_1.pin_42, S1.Pin_1, S1.Pin_2, S2.Pin_1, S2.Pin_2, S3.Pin_1, S3.Pin_2, S4.Pin_1, S4.Pin_2, LED4.anode, R3.Pin_1, R4.Pin_1, R5.Pin_1, J1.gnd
  N2: Pico/Pico2_Mod_1.pin_17, S2.Pin_3, S2.Pin_4
  N3: Pico/Pico2_Mod_1.pin_19, S3.Pin_3, S3.Pin_4
  N4: Pico/Pico2_Mod_1.pin_20, S4.Pin_3, S4.Pin_4
  N5: Pico/Pico2_Mod_1.pin_21, LED1.anode
  N6: Pico/Pico2_Mod_1.pin_22, LED2.anode
  N7: Pico/Pico2_Mod_1.pin_30, S1.Pin_3, S1.Pin_4
  N8: Pico/Pico2_Mod_1.pin_36, J1.vcc
  N9: LED1.cathode, R5.Pin_0
  N10: LED2.cathode, R4.Pin_0
  N11: LED4.cathode, R3.Pin_0

custom parts:
  Raspberry Pi Pico or Pico 2: Raspberry Pi Pico and Pico 2. Based around the RP2040 and RP2350 microcontrollers respectively, Picos are low cost microcontroller device bringing Raspberry Pi quality, cost, and easy of use to the microcontroller space. Jan 2021, Split part in to two versions: tht (this one) and SMD. This one will drill holes for a .1 in header in pcb to allow plugging in the module as well as providing pads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
  DHT11 module: https://cdn-learn.adafruit.com/downloads/pdf/dht.pdf DHT11 black pcb module reference by:https://github.com/adafruit/Fritzing-Library/blob/master/parts/DHT11%20Humitidy%20and%20Temperature%20Sensor.fzpz
